// Logisim project PROIECT_FIFO.circ as structural Verilog
module main (
  input  pop,
  input  push,
  input  [3:0] in_3,
  input  in_4,
  input  reset,
  input  in_6,
  input  in_7,
  input  in_8,
  input  in_9,
  input  in_10,
  input  in_11,
  input  in_12,
  input  in_13,
  input  in_14,
  input  [3:0] in_15,
  input  in_16,
  input  in_17,
  input  in_18,
  input  in_19,
  input  in_20,
  input  in_21,
  input  in_22,
  input  in_23,
  input  in_24,
  input  in_25,
  output [7:0] out_26,
  output [6:0] out_27,
  output [31:0] TEST,
  output [3:0] out_29,
  output out_30,
  output out_31,
  output we,
  output out_33,
  output re,
  output [3:0] out_35,
  output [3:0] out_36
);

  wire and_1_out, and_2_out, and_3_out, and_5_out, clock_1_out, not_1_out, not_2_out, not_3_out, START_out;
  wire [3:0] d_ff_5_q, d_ff_8_q;
  wire [31:0] ram_proj_1_y_ram;

  Button START (.out(START_out));
  data data_1 (
    .start(START_out), .push(push), .pop(pop), .clk100(START_out), .reset(reset), .input_0(in_6),
    .Input_1(in_7), .Input_2(in_9), .Input_3(in_10), .Input_4(in_11), .Input_5(in_12), .Input_6(in_13),
    .Input_7(in_14), .Input_8(in_16), .Input_9(in_18), .Input_10(in_19), .Input_11(in_20), .Input_12(in_22),
    .Input_13(in_23), .Input_14(in_24), .Input_15(in_25), .rez(TEST));
  Clock clock_1 (.out(clock_1_out));
  States states_1 (.POP(pop), .PUSH(push), .CLOCK(clock_1_out), .EMPTY(out_30), .LAST(out_31), .FULL(out_33));
  not not_1 (not_1_out, push);
  and and_1 (and_1_out, pop, clock_1_out);
  and and_2 (and_2_out, not_1_out, pop);
  not not_2 (not_2_out, out_30);
  and and_3 (and_3_out, push, clock_1_out);
  not not_3 (not_3_out, out_33);
  and and_4 (re, not_2_out, and_2_out);
  and and_5 (and_5_out, re, and_1_out);
  and and_6 (we, not_3_out, push);
  counterproj counterproj_1 (
    .Data(in_3), .Direction(in_4), .Reset(START_out), .CLOCK(and_3_out), .LOAD(in_8), .Output(out_35));
  counterproj counterproj_2 (
    .Data(in_15), .Direction(in_17), .Reset(START_out), .CLOCK(and_5_out), .LOAD(in_21), .Output(out_36));
  Ram_Proj ram_proj_1 (
    .A_RAM(out_29), .CS_RAM(not_3_out), .WE(we), .D_RAM(TEST), .CLOCK(clock_1_out), .Y_RAM(ram_proj_1_y_ram));
  D_Flip_Flop d_ff_1 (.D(out_35[3]), .clk(and_3_out), .Q(d_ff_5_q[3]));  // open: Qn, preset, reset
  D_Flip_Flop d_ff_2 (.D(out_35[2]), .clk(and_3_out), .Q(d_ff_5_q[2]));  // open: Qn, preset, reset
  D_Flip_Flop d_ff_3 (.D(out_36[3]), .clk(and_5_out), .Q(d_ff_8_q[3]));  // open: Qn, preset, reset
  D_Flip_Flop d_ff_4 (.D(out_35[1]), .clk(and_3_out), .Q(d_ff_5_q[1]));  // open: Qn, preset, reset
  D_Flip_Flop d_ff_5 (.D(out_35[0]), .clk(and_3_out), .Q(d_ff_5_q[0]));  // open: Qn, preset, reset
  D_Flip_Flop d_ff_6 (.D(out_36[2]), .clk(and_5_out), .Q(d_ff_8_q[2]));  // open: Qn, preset, reset
  DISPLAY display_1 (
    .datain32(ram_proj_1_y_ram), .clk(clock_1_out), .reset(START_out), .anodes(out_26), .cathodes(out_27));
  D_Flip_Flop d_ff_7 (.D(out_36[1]), .clk(and_5_out), .Q(d_ff_8_q[1]));  // open: Qn, preset, reset
  D_Flip_Flop d_ff_8 (.D(out_36[0]), .clk(and_5_out), .Q(d_ff_8_q[0]));  // open: Qn, preset, reset
  mux2_1 mux2_1_1 (.in1(d_ff_5_q), .in2(d_ff_8_q), .sel(re), .rez(out_29));
endmodule

module DISPLAY (
  input  [31:0] datain32,
  input  clk,
  input  reset,
  output [7:0] anodes,
  output [6:0] cathodes
);

  wire [6:0] binary_to_7seg_1_display_value, binary_to_7seg_1_display_value_2,
       binary_to_7seg_2_display_value, binary_to_7seg_2_display_value_2, binary_to_7seg_3_display_value,
       binary_to_7seg_3_display_value_2, binary_to_7seg_4_display_value, binary_to_7seg_4_display_value_2;

  BINARY_TO_7SEG binary_to_7seg_1 (.binary_number(datain32[3:0]), .display_value(binary_to_7seg_1_display_value));
  BINARY_TO_7SEG binary_to_7seg_2 (.binary_number(datain32[7:4]), .display_value(binary_to_7seg_2_display_value_2));
  BINARY_TO_7SEG binary_to_7seg_3 (.binary_number(datain32[11:8]), .display_value(binary_to_7seg_3_display_value_2));
  BINARY_TO_7SEG binary_to_7seg_4 (.binary_number(datain32[15:12]), .display_value(binary_to_7seg_4_display_value));
  BINARY_TO_7SEG binary_to_7seg_1_dup2 (
    .binary_number(datain32[19:16]), .display_value(binary_to_7seg_1_display_value_2));
  BINARY_TO_7SEG binary_to_7seg_2_dup2 (
    .binary_number(datain32[23:20]), .display_value(binary_to_7seg_2_display_value));
  BINARY_TO_7SEG binary_to_7seg_3_dup2 (
    .binary_number(datain32[27:24]), .display_value(binary_to_7seg_3_display_value));
  BINARY_TO_7SEG binary_to_7seg_4_dup2 (
    .binary_number(datain32[31:28]), .display_value(binary_to_7seg_4_display_value_2));
  display_unit display_unit_1 (
    .data1(binary_to_7seg_1_display_value), .data2(binary_to_7seg_2_display_value_2),
    .data3(binary_to_7seg_3_display_value_2), .data4(binary_to_7seg_4_display_value),
    .data5(binary_to_7seg_1_display_value_2), .data6(binary_to_7seg_2_display_value),
    .data7(binary_to_7seg_3_display_value), .data8(binary_to_7seg_4_display_value_2), .clk(clk),
    .reset(reset), .anodes(anodes), .cathodes(cathodes));
endmodule

module fifo_only (
  input  pop,
  input  push,
  input  clk100,
  input  reset,
  output empty,
  output last,
  output full
);

  wire f_div_new_1_clk_out;

  States states_1 (.POP(pop), .PUSH(push), .CLOCK(f_div_new_1_clk_out), .EMPTY(empty), .LAST(last), .FULL(full));
  F_DIV_new f_div_new_1 (.CLK_in(clk100), .RESET(reset), .CLK_out(f_div_new_1_clk_out));
endmodule

module data (
  input  start,
  input  push,
  input  pop,
  input  clk100,
  input  reset,
  input  input_0,
  input  Input_1,
  input  Input_2,
  input  Input_3,
  input  Input_4,
  input  Input_5,
  input  Input_6,
  input  Input_7,
  input  Input_8,
  input  Input_9,
  input  Input_10,
  input  Input_11,
  input  Input_12,
  input  Input_13,
  input  Input_14,
  input  Input_15,
  output [31:0] rez
);

  wire debouncer_1_y, debouncer_2_y, debouncer_3_y, f_div_1_clk_out, or_1_out, or_2_out;
  wire [3:0] counterproj_1_output, decoder_1_outp;

  F_DIV f_div_1 (.CLK_in(clk100), .RESET(reset), .CLK_out(f_div_1_clk_out));
  DEBOUNCER debouncer_1 (.BUTON(start), .CLK(f_div_1_clk_out), .Y(debouncer_1_y));
  DEBOUNCER debouncer_2 (.BUTON(push), .CLK(f_div_1_clk_out), .Y(debouncer_2_y));
  DEBOUNCER debouncer_3 (.BUTON(pop), .CLK(f_div_1_clk_out), .Y(debouncer_3_y));
  or or_1 (or_1_out, debouncer_2_y, debouncer_1_y, debouncer_3_y);
  or or_2 (or_2_out, input_0, Input_1, Input_2, Input_3, Input_4, Input_5, Input_6, Input_7, Input_8, Input_9, Input_10, Input_11, Input_12, Input_13, Input_14, Input_15);
  counterproj counterproj_1 (
    .Data(4'b0000), .Direction(1'b0), .Reset(or_1_out), .CLOCK(or_2_out), .LOAD(1'b0),
    .Output(counterproj_1_output));
  decoder decoder_1 (
    .I0(input_0), .I1(Input_1), .I2(Input_2), .I3(Input_3), .I4(Input_4), .I5(Input_5), .I6(Input_6),
    .I7(Input_7), .I8(Input_8), .I9(Input_9), .Ia(Input_10), .Ib(Input_11), .Ic(Input_12), .Id(Input_13),
    .Ie(Input_14), .Iff(Input_15), .outp(decoder_1_outp));
  store_data store_data_1 (.reset(or_1_out), .datain(decoder_1_outp), .addr(counterproj_1_output), .dataout(rez));
endmodule

module TEST (
  input  START,
  input  PUSH,
  input  pop,
  input  Input_1,
  input  Input_2,
  input  Input_3,
  input  Input_4,
  input  Input_5,
  input  Input_6,
  input  Input_7,
  input  Input_8,
  input  Input_9,
  input  Input_10,
  output [3:0] Output_bus_1,
  output [6:0] Output_bus_2,
  output [3:0] ADDRESS,
  output EMPTY,
  output LAST,
  output we,
  output FULL,
  output re
);

  wire and_1_out, and_2_out, and_3_out, and_5_out, clock_1_out, not_1_out, not_2_out, not_3_out, not_4_out;
  wire [3:0] counterproj_1_output, counterproj_2_output, d_ff_5_q, d_ff_8_q;
  wire [31:0] data_1_rez, ram_proj_1_y_ram;

  data data_1 (
    .start(START), .push(pop), .pop(PUSH), .clk100(Input_1), .reset(Input_2), .input_0(Input_3),
    .Input_1(Input_4), .Input_2(Input_5), .Input_3(Input_6), .Input_4(Input_7), .Input_5(Input_8),
    .Input_6(Input_9), .Input_7(Input_10), .Input_8(Input_10), .Input_9(Input_10), .Input_10(Input_10),
    .Input_11(Input_10), .Input_12(Input_10), .Input_13(Input_10), .rez(data_1_rez));  // open: Input_14, Input_15
  Clock clock_1 (.out(clock_1_out));
  States states_1 (.POP(PUSH), .PUSH(pop), .CLOCK(clock_1_out), .EMPTY(EMPTY), .LAST(LAST), .FULL(FULL));
  not not_1 (not_1_out, pop);
  and and_1 (and_1_out, PUSH, clock_1_out);
  and and_2 (and_2_out, not_1_out, PUSH);
  not not_2 (not_2_out, FULL);
  not not_3 (not_3_out, EMPTY);
  and and_3 (and_3_out, pop, clock_1_out);
  and and_4 (re, not_3_out, and_2_out);
  and and_5 (and_5_out, re, and_1_out);
  and and_6 (we, not_2_out, pop);
  counterproj counterproj_1 (
    .Data(4'b0000), .Direction(1'b0), .Reset(START), .CLOCK(and_3_out), .LOAD(1'b0),
    .Output(counterproj_1_output));
  counterproj counterproj_2 (
    .Data(4'b0000), .Direction(1'b0), .Reset(START), .CLOCK(and_5_out), .LOAD(1'b0),
    .Output(counterproj_2_output));
  Ram_Proj ram_proj_1 (
    .A_RAM(ADDRESS), .CS_RAM(not_2_out), .WE(we), .D_RAM(data_1_rez), .CLOCK(clock_1_out),
    .Y_RAM(ram_proj_1_y_ram));
  D_Flip_Flop d_ff_1 (.D(counterproj_1_output[3]), .clk(and_3_out), .Q(d_ff_5_q[3]));  // open: Qn, preset, reset
  D_Flip_Flop d_ff_2 (.D(counterproj_1_output[2]), .clk(and_3_out), .Q(d_ff_5_q[2]));  // open: Qn, preset, reset
  D_Flip_Flop d_ff_3 (.D(counterproj_1_output[1]), .clk(and_3_out), .Q(d_ff_5_q[1]));  // open: Qn, preset, reset
  D_Flip_Flop d_ff_4 (.D(counterproj_2_output[3]), .clk(and_5_out), .Q(d_ff_8_q[3]));  // open: Qn, preset, reset
  D_Flip_Flop d_ff_5 (.D(counterproj_1_output[0]), .clk(and_3_out), .Q(d_ff_5_q[0]));  // open: Qn, preset, reset
  D_Flip_Flop d_ff_6 (.D(counterproj_2_output[2]), .clk(and_5_out), .Q(d_ff_8_q[2]));  // open: Qn, preset, reset
  DISPLAY_BASYS3 DISPLAY_BASYS3_1 (
    .DATA32(ram_proj_1_y_ram), .clk(clock_1_out), .reset(START), .anodes(Output_bus_1),
    .cathodes(Output_bus_2));
  D_Flip_Flop d_ff_7 (.D(counterproj_2_output[1]), .clk(and_5_out), .Q(d_ff_8_q[1]));  // open: Qn, preset, reset
  not not_4 (not_4_out, pop);
  D_Flip_Flop d_ff_8 (.D(counterproj_2_output[0]), .clk(and_5_out), .Q(d_ff_8_q[0]));  // open: Qn, preset, reset
  mux2_1 mux2_1_1 (.in1(d_ff_5_q), .in2(d_ff_8_q), .sel(not_4_out), .rez(ADDRESS));
endmodule

module DISPLAY_BASYS3 (
  input  [31:0] DATA32,
  input  clk,
  input  reset,
  output [3:0] anodes,
  output [6:0] cathodes
);

  wire [6:0] binary_to_7seg_1_display_value, binary_to_7seg_2_display_value, binary_to_7seg_3_display_value,
       binary_to_7seg_4_display_value, binary_to_7seg_5_display_value, binary_to_7seg_6_display_value,
       binary_to_7seg_7_display_value, binary_to_7seg_8_display_value;

  BINARY_TO_7SEG binary_to_7seg_1 (.binary_number(DATA32[3:0]), .display_value(binary_to_7seg_1_display_value));
  BINARY_TO_7SEG binary_to_7seg_2 (.binary_number(DATA32[7:4]), .display_value(binary_to_7seg_2_display_value));
  BINARY_TO_7SEG binary_to_7seg_3 (.binary_number(DATA32[11:8]), .display_value(binary_to_7seg_3_display_value));
  BINARY_TO_7SEG binary_to_7seg_4 (.binary_number(DATA32[15:12]), .display_value(binary_to_7seg_4_display_value));
  BINARY_TO_7SEG binary_to_7seg_5 (.binary_number(DATA32[19:16]), .display_value(binary_to_7seg_5_display_value));
  BINARY_TO_7SEG binary_to_7seg_6 (.binary_number(DATA32[23:20]), .display_value(binary_to_7seg_6_display_value));
  BINARY_TO_7SEG binary_to_7seg_7 (.binary_number(DATA32[27:24]), .display_value(binary_to_7seg_7_display_value));
  BINARY_TO_7SEG binary_to_7seg_8 (.binary_number(DATA32[31:28]), .display_value(binary_to_7seg_8_display_value));
  displayBASYS3 displaybasys3_1 (
    .data1(binary_to_7seg_1_display_value), .data2(binary_to_7seg_2_display_value),
    .data3(binary_to_7seg_3_display_value), .data4(binary_to_7seg_4_display_value),
    .data5(binary_to_7seg_5_display_value), .data6(binary_to_7seg_6_display_value),
    .data7(binary_to_7seg_7_display_value), .data8(binary_to_7seg_8_display_value), .clk(clk), .reset(reset),
    .anodes(anodes), .cathodes(cathodes));
endmodule

module SIMULATION (
  input  pop,
  input  push,
  input  input_new,
  input  in_4,
  input  in_5,
  input  in_6,
  input  [3:0] in_7,
  input  in_8,
  input  in_9,
  input  in_10,
  input  in_11,
  input  in_12,
  input  in_13,
  input  in_14,
  input  in_15,
  input  in_16,
  input  in_17,
  input  in_18,
  input  [3:0] in_19,
  input  in_20,
  input  in_21,
  input  in_22,
  input  in_23,
  input  in_24,
  input  in_25,
  input  in_26,
  output [31:0] out_27,
  output [31:0] TEST,
  output [3:0] out_29,
  output out_30,
  output out_31,
  output we,
  output out_33,
  output re,
  output [3:0] out_35,
  output [3:0] out_36
);

  wire and_1_out, and_2_out, and_3_out, and_6_out, clock_1_out, not_1_out, not_2_out, not_3_out, not_4_out,
       START_out;
  wire [3:0] d_ff_5_q, d_ff_8_q;
  wire [6:0] binary_to_7seg_1_display_value, binary_to_7seg_2_display_value, binary_to_7seg_3_display_value,
       binary_to_7seg_4_display_value, binary_to_7seg_5_display_value, binary_to_7seg_6_display_value,
       binary_to_7seg_7_display_value, binary_to_7seg_8_display_value;

  Button START (.out(START_out));
  data_simulation data_simulation_1 (
    .start(input_new), .clk100(in_4), .input_0(in_5), .Input_1(in_6), .Input_2(in_8), .Input_3(in_10),
    .Input_4(in_11), .Input_5(in_12), .Input_6(in_14), .Input_7(in_15), .Input_8(in_16), .Input_9(in_17),
    .Input_10(in_18), .Input_11(in_20), .Input_12(in_22), .Input_13(in_23), .Input_14(in_24),
    .Input_15(in_26), .rez(TEST));  // open: out_20, out_21
  Clock clock_1 (.out(clock_1_out));
  States states_1 (.POP(pop), .PUSH(push), .CLOCK(clock_1_out), .EMPTY(out_30), .LAST(out_31), .FULL(out_33));
  not not_1 (not_1_out, push);
  and and_1 (and_1_out, pop, clock_1_out);
  and and_2 (and_2_out, not_1_out, pop);
  not not_2 (not_2_out, out_33);
  not not_3 (not_3_out, out_30);
  and and_3 (and_3_out, push, clock_1_out);
  and and_4 (we, not_2_out, push);
  and and_5 (re, not_3_out, and_2_out);
  and and_6 (and_6_out, re, and_1_out);
  not not_4 (not_4_out, re);
  Ram_Proj ram_proj_1 (
    .A_RAM(out_29), .CS_RAM(not_2_out), .WE(not_4_out), .D_RAM(TEST), .CLOCK(clock_1_out), .Y_RAM(out_27));
  counterproj counterproj_1 (
    .Data(in_7), .Direction(in_9), .Reset(START_out), .CLOCK(and_3_out), .LOAD(in_13), .Output(out_35));
  counterproj counterproj_2 (
    .Data(in_19), .Direction(in_21), .Reset(START_out), .CLOCK(and_6_out), .LOAD(in_25), .Output(out_36));
  D_Flip_Flop d_ff_1 (.D(out_35[3]), .clk(and_3_out), .Q(d_ff_5_q[3]));  // open: Qn, preset, reset
  D_Flip_Flop d_ff_2 (.D(out_35[2]), .clk(and_3_out), .Q(d_ff_5_q[2]));  // open: Qn, preset, reset
  D_Flip_Flop d_ff_3 (.D(out_35[1]), .clk(and_3_out), .Q(d_ff_5_q[1]));  // open: Qn, preset, reset
  D_Flip_Flop d_ff_4 (.D(out_36[3]), .clk(and_6_out), .Q(d_ff_8_q[3]));  // open: Qn, preset, reset
  D_Flip_Flop d_ff_5 (.D(out_35[0]), .clk(and_3_out), .Q(d_ff_5_q[0]));  // open: Qn, preset, reset
  D_Flip_Flop d_ff_6 (.D(out_36[2]), .clk(and_6_out), .Q(d_ff_8_q[2]));  // open: Qn, preset, reset
  BINARY_TO_7SEG binary_to_7seg_1 (.binary_number(out_27[3:0]), .display_value(binary_to_7seg_1_display_value));
  D_Flip_Flop d_ff_7 (.D(out_36[1]), .clk(and_6_out), .Q(d_ff_8_q[1]));  // open: Qn, preset, reset
  D_Flip_Flop d_ff_8 (.D(out_36[0]), .clk(and_6_out), .Q(d_ff_8_q[0]));  // open: Qn, preset, reset
  _7_Segment_Display u_7_segment_display_1 (
    .g(binary_to_7seg_1_display_value[0]), .f(binary_to_7seg_1_display_value[1]),
    .a(binary_to_7seg_1_display_value[6]), .b(binary_to_7seg_1_display_value[5]),
    .e(binary_to_7seg_1_display_value[2]), .d(binary_to_7seg_1_display_value[3]),
    .c(binary_to_7seg_1_display_value[4]));  // open: dp
  mux2_1 mux2_1_1 (.in1(d_ff_5_q), .in2(d_ff_8_q), .sel(re), .rez(out_29));
  BINARY_TO_7SEG binary_to_7seg_2 (.binary_number(out_27[7:4]), .display_value(binary_to_7seg_2_display_value));
  _7_Segment_Display u_7_segment_display_2 (
    .g(binary_to_7seg_2_display_value[0]), .f(binary_to_7seg_2_display_value[1]),
    .a(binary_to_7seg_2_display_value[6]), .b(binary_to_7seg_2_display_value[5]),
    .e(binary_to_7seg_2_display_value[2]), .d(binary_to_7seg_2_display_value[3]),
    .c(binary_to_7seg_2_display_value[4]));  // open: dp
  BINARY_TO_7SEG binary_to_7seg_3 (.binary_number(out_27[11:8]), .display_value(binary_to_7seg_3_display_value));
  BINARY_TO_7SEG binary_to_7seg_7 (.binary_number(out_27[27:24]), .display_value(binary_to_7seg_7_display_value));
  BINARY_TO_7SEG binary_to_7seg_8 (.binary_number(out_27[31:28]), .display_value(binary_to_7seg_8_display_value));
  BINARY_TO_7SEG binary_to_7seg_4 (.binary_number(out_27[15:12]), .display_value(binary_to_7seg_4_display_value));
  BINARY_TO_7SEG binary_to_7seg_5 (.binary_number(out_27[19:16]), .display_value(binary_to_7seg_5_display_value));
  BINARY_TO_7SEG binary_to_7seg_6 (.binary_number(out_27[23:20]), .display_value(binary_to_7seg_6_display_value));
  _7_Segment_Display u_7_segment_display_3 (
    .g(binary_to_7seg_3_display_value[0]), .f(binary_to_7seg_3_display_value[1]),
    .a(binary_to_7seg_3_display_value[6]), .b(binary_to_7seg_3_display_value[5]),
    .e(binary_to_7seg_3_display_value[2]), .d(binary_to_7seg_3_display_value[3]),
    .c(binary_to_7seg_3_display_value[4]));  // open: dp
  _7_Segment_Display u_7_segment_display_4 (
    .g(binary_to_7seg_7_display_value[0]), .f(binary_to_7seg_7_display_value[1]),
    .a(binary_to_7seg_7_display_value[6]), .b(binary_to_7seg_7_display_value[5]),
    .e(binary_to_7seg_7_display_value[2]), .d(binary_to_7seg_7_display_value[3]),
    .c(binary_to_7seg_7_display_value[4]));  // open: dp
  _7_Segment_Display u_7_segment_display_5 (
    .g(binary_to_7seg_8_display_value[0]), .f(binary_to_7seg_8_display_value[1]),
    .a(binary_to_7seg_8_display_value[6]), .b(binary_to_7seg_8_display_value[5]),
    .e(binary_to_7seg_8_display_value[2]), .d(binary_to_7seg_8_display_value[3]),
    .c(binary_to_7seg_8_display_value[4]));  // open: dp
  _7_Segment_Display u_7_segment_display_6 (
    .g(binary_to_7seg_4_display_value[0]), .f(binary_to_7seg_4_display_value[1]),
    .a(binary_to_7seg_4_display_value[6]), .b(binary_to_7seg_4_display_value[5]),
    .e(binary_to_7seg_4_display_value[2]), .d(binary_to_7seg_4_display_value[3]),
    .c(binary_to_7seg_4_display_value[4]));  // open: dp
  _7_Segment_Display u_7_segment_display_7 (
    .g(binary_to_7seg_5_display_value[0]), .f(binary_to_7seg_5_display_value[1]),
    .a(binary_to_7seg_5_display_value[6]), .b(binary_to_7seg_5_display_value[5]),
    .e(binary_to_7seg_5_display_value[2]), .d(binary_to_7seg_5_display_value[3]),
    .c(binary_to_7seg_5_display_value[4]));  // open: dp
  _7_Segment_Display u_7_segment_display_8 (
    .g(binary_to_7seg_6_display_value[0]), .f(binary_to_7seg_6_display_value[1]),
    .a(binary_to_7seg_6_display_value[6]), .b(binary_to_7seg_6_display_value[5]),
    .e(binary_to_7seg_6_display_value[2]), .d(binary_to_7seg_6_display_value[3]),
    .c(binary_to_7seg_6_display_value[4]));  // open: dp
endmodule

module ram_only (
  input  [3:0] address,
  input  csc,
  input  we,
  input  [31:0] data,
  input  clk,
  output [31:0] outp
);

  Ram_Proj ram_proj_1 (.A_RAM(address), .CS_RAM(csc), .WE(we), .D_RAM(data), .CLOCK(clk), .Y_RAM(outp));
endmodule

module counter_only (
  input  push,
  input  res,
  input  load,
  input  re,
  input  clk100,
  input  pop,
  output [3:0] rez
);

  wire and_1_out, and_2_out, debouncer_1_y, debouncer_2_y, f_div_1_clk_out;
  wire [3:0] counterproj_1_output, counterproj_2_output, d_ff_1_q, d_ff_2_q;

  F_DIV f_div_1 (.CLK_in(clk100), .RESET(1'b0), .CLK_out(f_div_1_clk_out));
  DEBOUNCER debouncer_1 (.BUTON(push), .CLK(f_div_1_clk_out), .Y(debouncer_1_y));
  and and_1 (and_1_out, debouncer_1_y, f_div_1_clk_out);
  and and_2 (and_2_out, debouncer_2_y, f_div_1_clk_out);
  DEBOUNCER debouncer_2 (.BUTON(pop), .CLK(f_div_1_clk_out), .Y(debouncer_2_y));
  counterproj counterproj_1 (
    .Data(4'b0000), .Direction(1'b0), .Reset(res), .CLOCK(and_1_out), .LOAD(load),
    .Output(counterproj_1_output));
  counterproj counterproj_2 (
    .Data(4'b0000), .Direction(1'b0), .Reset(res), .CLOCK(and_2_out), .LOAD(1'b0),
    .Output(counterproj_2_output));
  D_Flip_Flop d_ff_1 (.D(counterproj_1_output[3]), .clk(and_1_out), .Q(d_ff_1_q[0]));  // open: Qn, preset, reset
  D_Flip_Flop d_ff_2 (.D(counterproj_2_output[3]), .clk(and_2_out), .Q(d_ff_2_q[0]));  // open: Qn, preset, reset
  D_Flip_Flop d_ff_3 (.D(counterproj_1_output[2]), .clk(and_1_out), .Q(d_ff_1_q[1]));  // open: Qn, preset, reset
  D_Flip_Flop d_ff_4 (.D(counterproj_2_output[2]), .clk(and_2_out), .Q(d_ff_2_q[1]));  // open: Qn, preset, reset
  D_Flip_Flop d_ff_5 (.D(counterproj_1_output[1]), .clk(and_1_out), .Q(d_ff_1_q[2]));  // open: Qn, preset, reset
  D_Flip_Flop d_ff_6 (.D(counterproj_2_output[1]), .clk(and_2_out), .Q(d_ff_2_q[2]));  // open: Qn, preset, reset
  D_Flip_Flop d_ff_7 (.D(counterproj_1_output[0]), .clk(and_1_out), .Q(d_ff_1_q[3]));  // open: Qn, preset, reset
  D_Flip_Flop d_ff_8 (.D(counterproj_2_output[0]), .clk(and_2_out), .Q(d_ff_2_q[3]));  // open: Qn, preset, reset
  mux2_1 mux2_1_1 (.in1(d_ff_1_q), .in2(d_ff_2_q), .sel(re), .rez(rez));
endmodule

module FIFO_compact (
  input  [31:0] datain,
  input  pop,
  input  push,
  input  start,
  input  clk100,
  output [7:0] out_6,
  output [6:0] out_7,
  output empty,
  output last,
  output full
);

  wire not_1_out, re_we_1_re, re_we_1_we;
  wire [3:0] counter_only_1_rez;
  wire [31:0] ram_proj_1_y_ram;

  counter_only counter_only_1 (
    .push(push), .res(start), .load(1'b0), .re(re_we_1_re), .clk100(clk100), .pop(pop),
    .rez(counter_only_1_rez));
  states_compact states_compact_1 (
    .pop(pop), .push(push), .clk100(clk100), .reset(start), .empty(empty), .last(last), .full(full));
  not not_1 (not_1_out, full);
  re_we re_we_1 (.full(full), .push(push), .pop(pop), .empty(empty), .we(re_we_1_we), .re(re_we_1_re));
  Ram_Proj ram_proj_1 (
    .A_RAM(counter_only_1_rez), .CS_RAM(not_1_out), .WE(re_we_1_we), .D_RAM(datain), .CLOCK(clk100),
    .Y_RAM(ram_proj_1_y_ram));
  DISPLAY display_1 (.datain32(ram_proj_1_y_ram), .clk(clk100), .reset(start), .anodes(out_6), .cathodes(out_7));
endmodule

module re_we (
  input  full,
  input  push,
  input  pop,
  input  empty,
  output we,
  output re
);

  wire and_2_out, not_1_out, not_2_out, not_3_out;

  not not_1 (not_1_out, full);
  not not_2 (not_2_out, push);
  not not_3 (not_3_out, empty);
  and and_1 (we, not_1_out, push);
  and and_2 (and_2_out, not_2_out, pop);
  and and_3 (re, and_2_out, not_3_out);
endmodule

module states_compact (
  input  pop,
  input  push,
  input  clk100,
  input  reset,
  output empty,
  output last,
  output full
);

  wire f_div_new_1_clk_out;

  F_DIV_new f_div_new_1 (.CLK_in(clk100), .RESET(reset), .CLK_out(f_div_new_1_clk_out));
  States states_1 (.POP(pop), .PUSH(push), .CLOCK(f_div_new_1_clk_out), .EMPTY(empty), .LAST(last), .FULL(full));
endmodule

module data_simulation (
  input  start,
  input  clk100,
  input  input_0,
  input  Input_1,
  input  Input_2,
  input  Input_3,
  input  Input_4,
  input  Input_5,
  input  Input_6,
  input  Input_7,
  input  Input_8,
  input  Input_9,
  input  Input_10,
  input  Input_11,
  input  Input_12,
  input  Input_13,
  input  Input_14,
  input  Input_15,
  output [31:0] rez,
  output [7:0] out_20,
  output [6:0] out_21
);

  wire or_1_out;
  wire [3:0] counterproj_1_output, decoder_1_outp;
  wire [6:0] binary_to_7seg_1_display_value, binary_to_7seg_2_display_value, binary_to_7seg_3_display_value,
       binary_to_7seg_4_display_value, binary_to_7seg_5_display_value, binary_to_7seg_6_display_value,
       binary_to_7seg_7_display_value, binary_to_7seg_8_display_value;

  or or_1 (or_1_out, input_0, Input_1, Input_2, Input_3, Input_4, Input_5, Input_6, Input_7, Input_8, Input_9, Input_10, Input_11, Input_12, Input_13, Input_14, Input_15);
  counterproj counterproj_1 (
    .Data(4'b0000), .Direction(1'b0), .Reset(start), .CLOCK(or_1_out), .LOAD(1'b0),
    .Output(counterproj_1_output));
  decoder decoder_1 (
    .I0(input_0), .I1(Input_1), .I2(Input_2), .I3(Input_3), .I4(Input_4), .I5(Input_5), .I6(Input_6),
    .I7(Input_7), .I8(Input_8), .I9(Input_9), .Ia(Input_10), .Ib(Input_11), .Ic(Input_12), .Id(Input_13),
    .Ie(Input_14), .Iff(Input_15), .outp(decoder_1_outp));
  store_data store_data_1 (.reset(start), .datain(decoder_1_outp), .addr(counterproj_1_output), .dataout(rez));
  BINARY_TO_7SEG binary_to_7seg_1 (.binary_number(rez[3:0]), .display_value(binary_to_7seg_1_display_value));
  BINARY_TO_7SEG binary_to_7seg_2 (.binary_number(rez[7:4]), .display_value(binary_to_7seg_2_display_value));
  BINARY_TO_7SEG binary_to_7seg_3 (.binary_number(rez[11:8]), .display_value(binary_to_7seg_3_display_value));
  BINARY_TO_7SEG binary_to_7seg_4 (.binary_number(rez[15:12]), .display_value(binary_to_7seg_4_display_value));
  BINARY_TO_7SEG binary_to_7seg_5 (.binary_number(rez[19:16]), .display_value(binary_to_7seg_5_display_value));
  BINARY_TO_7SEG binary_to_7seg_6 (.binary_number(rez[23:20]), .display_value(binary_to_7seg_6_display_value));
  BINARY_TO_7SEG binary_to_7seg_7 (.binary_number(rez[27:24]), .display_value(binary_to_7seg_7_display_value));
  BINARY_TO_7SEG binary_to_7seg_8 (.binary_number(rez[31:28]), .display_value(binary_to_7seg_8_display_value));
  display_unit display_unit_1 (
    .data1(binary_to_7seg_1_display_value), .data2(binary_to_7seg_2_display_value),
    .data3(binary_to_7seg_3_display_value), .data4(binary_to_7seg_4_display_value),
    .data5(binary_to_7seg_5_display_value), .data6(binary_to_7seg_6_display_value),
    .data7(binary_to_7seg_7_display_value), .data8(binary_to_7seg_8_display_value), .clk(clk100),
    .reset(start), .anodes(out_20), .cathodes(out_21));
endmodule

// VHDL entity States, as the project stores it:
LIBRARY ieee;
USE ieee.std_logic_1164.all;


ENTITY States IS
  PORT (
  POP: in std_logic;
  		PUSH: in std_logic;
  		CLOCK:in std_logic;
  		EMPTY, LAST, FULL: out std_logic
 
    );
END States;



ARCHITECTURE ARCH OF States IS

type state_m is (st0, st1,st2,st3,st4,st5,st6,st7,st8,st9,st10,st11,st12,st13,st14,st15,st16);
signal state, nextstate : state_m; 
BEGIN
		state_act: process (CLOCK)
		begin
			if clock'event and clock='1' then
				state<=nextstate;
			end if;
		end process;
				
		transition: process(state,pop,push)
		begin

		EMPTY<='0' ;LAST<= '0'; FULL<= '0';
		
		case state is
			when st0 => EMPTY <= '1';
				if POP = '1' then nextstate <= st0;
				elsif PUSH = '1' then nextstate <= st1;
				else nextstate <= st0;
				end if;
			when st1 =>
				if POP = '1' then nextstate <= st0;
				elsif PUSH = '0' then nextstate <= st1;
				else nextstate <= st2;
				end if;
			when st2 =>
				if POP = '1' then nextstate <= st1;
				elsif PUSH = '0' then nextstate <= st2;
				else nextstate <= st3;
				end if;
			when st3 =>
				if POP = '1' then nextstate <= st2;
				elsif PUSH = '0' then nextstate <= st3;
				else nextstate <= st4;
				end if;
			when st4 =>
				if POP = '1' then nextstate <= st3;
				elsif PUSH = '0' then nextstate <= st4;
				else nextstate <= st5;
				end if;
			when st5 =>
				if POP = '1' then nextstate <= st4;
				elsif PUSH = '0' then nextstate <= st5;
				else nextstate <= st6;
				end if;
			when st6 =>
				if POP = '1' then nextstate <= st5;
				elsif PUSH = '0' then nextstate <= st6;
				else nextstate <= st7;
				end if;
			when st7 =>
				if POP = '1' then nextstate <= st6;
				elsif PUSH = '0' then nextstate <= st7;
				else nextstate <= st8;
				end if;
			when st8 =>
				if POP = '1' then nextstate <= st7;
				elsif PUSH = '0' then nextstate <= st8;
				else nextstate <= st9;
				end if;
			when st9 =>
				if POP = '1' then nextstate <= st8;
				elsif PUSH = '0' then nextstate <= st9;
				else nextstate <= st10;
				end if;
			when st10 =>
				if POP = '1' then nextstate <= st9;
				elsif PUSH = '0' then nextstate <= st10;
				else nextstate <= st11;
				end if;
			when st11 =>
				if POP = '1' then nextstate <= st10;
				elsif PUSH = '0' then nextstate <= st11;
				else nextstate <= st12;
				end if;
			when st12 =>
				if POP = '1' then nextstate <= st11;
				elsif PUSH = '0' then nextstate <= st12;
				else nextstate <= st13;
				end if;
			when st13 =>
				if POP = '1' then nextstate <= st12;
				elsif PUSH = '0' then nextstate <= st13;
				else nextstate <= st14;
				end if;
			when st14 =>
				if POP = '1' then nextstate <= st13;
				elsif PUSH = '0' then nextstate <= st14;
				else nextstate <= st15;
				end if;
			when st15 => LAST <= '1';
				if POP = '1' then nextstate <= st14;
				elsif PUSH = '0' then nextstate <= st15;
				else nextstate <= st16;
				end if;
			when st16 => FULL <= '1';
				if POP = '1' then nextstate <= st15;
				elsif PUSH = '0' then nextstate <= st2;
				else nextstate <= st1;
				end if;
			end case;
			end process transition;


END ARCH;

// VHDL entity Ram_Proj, as the project stores it:
--------------------------------------------------------------------------------
-- Project :
 --Fifo Memory
-- File    :
-- Autor   :
 --Balogh Flora
-- Date    :
 --15.05.2023.
--
--------------------------------------------------------------------------------
-- Description :
--
 --This is the Ram memory for my 1st year DSD project ehich is to implement a Fifo memory
--------------------------------------------------------------------------------


LIBRARY ieee;

use IEEE.STD_LOGIC_1164.all;
use IEEE.STD_LOGIC_UNSIGNED.all;

ENTITY Ram_Proj IS
  PORT (
  A_RAM: in std_logic_VECTOR (3 downto 0); --addresses
  CS_RAM: in std_logic; --chip selection signal, „Chip Select”
  WE: in std_logic; --signal for writing validation, „Write Enable”
  D_RAM: in std_logic_VECTOR(31 downto 0);
  Y_RAM: out std_logic_VECTOR(31 downto 0);
  CLOCK: IN std_logic
  );
END Ram_Proj;

ARCHITECTURE Behaviorial OF Ram_Proj IS
type MATRIX is array (0 to 15) of std_logic_vector(31 downto 0);
signal Mem: MATRIX := ( x"00000000",x"00000000",x"00000000",x"00000000",x"00000000", x"00000000",x"00000000",x"00000000",x"00000000",x"00000000",x"00000000",x"00000000",x"00000000",x"00000000",x"00000000",x"00000000");

BEGIN
 --Mem<=c;
 
process (CLOCK, CS_ram, A_ram, WE)
	begin
		if CLock = '1' and CLock'EVENT and CS_ram = '1' then
			if (WE = '1') then
				Mem (conv_integer(A_ram)) <= D_RAM;
			else
			Y_RAM <= Mem( conv_integer(A_ram) );
			end if;
		end if;
	end process;
 --Mem<=c;

END Behaviorial;

// VHDL entity counterproj, as the project stores it:
--------------------------------------------------------------------------------
-- Project :
-- File    :
-- Autor   :
-- Date    :
--
--------------------------------------------------------------------------------
-- Description :
--
--------------------------------------------------------------------------------
library IEEE; 
USE ieee.std_logic_1164.all;
USE ieee.numeric_std.all;

ENTITY counterproj IS
  PORT (
  	Data : in std_logic_VECTOR(3 DOWNTO 0);
  	Direction: in std_logic;
  	Reset: in std_logic;
  	Output: out std_logic_VECTOR(3 downto 0);
  	CLOCK: IN std_logic;
  	LOAD: IN STD_LOGIC
  	
    );
END counterproj;

--------------------------------------------------------------------------------
--Complete your VHDL description below
--------------------------------------------------------------------------------

ARCHITECTURE ARCH OF counterproj IS

signal temp: std_logic_VECTOR(3 DOWNTO 0);
BEGIN

process(Clock,Reset)
begin
if Reset='1' then
temp <= "0000";
elsif ( Clock'event and Clock='1') then
if Load='1' then
temp <= Data;
elsif (Load='0' and Direction='0') then
temp <= std_logic_vector(unsigned(temp) + 1);
elsif (Load='0' and Direction='1') then
temp <= std_logic_vector(unsigned(temp) - 1);
end if;
end if;
end process;
Output <= temp;
Output<= temp;
	

END ARCH;

// VHDL entity mux2_1, as the project stores it:
LIBRARY ieee;
USE ieee.std_logic_1164.all;

ENTITY mux2_1 IS
  PORT (
  in1, in2 :in std_logic_vector(3 downto 0);
  sel : in std_logic;
  rez: out std_logic_vector(3 downto 0)
    );
END mux2_1;


ARCHITECTURE behaviour OF mux2_1 IS

BEGIN
process (in1,in2, sel)
begin
	if sel = '0' then
	rez<=in1;
	else 
	rez<=in2;
	end if;
end process;
	


END behaviour;

// VHDL entity Decoder1, as the project stores it:
library IEEE;
use IEEE.STD_LOGIC_1164.ALL;
use IEEE.STD_LOGIC_ARITH.ALL;
use IEEE.STD_LOGIC_UNSIGNED.ALL;

entity Decoder1 is
    Port (
			     clk : in  STD_LOGIC;
                	Row : in  STD_LOGIC_VECTOR (3 downto 0);
			     Col : out  STD_LOGIC_VECTOR (3 downto 0);
                	DecodeOut : out  STD_LOGIC_VECTOR (3 downto 0));
end Decoder1;

architecture Behavioral of Decoder1 is

signal sclk :STD_LOGIC_VECTOR(19 downto 0);
begin
	process(clk)
		begin 
		if clk'event and clk = '1' then
			-- 1ms
			if sclk = "00011000011010100000" then 
				--C1
				Col<= "0111";
				sclk <= sclk+1;
			-- check row pins
			elsif sclk = "00011000011010101000" then	
				--R1
				if Row = "0111" then
					DecodeOut <= "0001";	--1
				--R2
				elsif Row = "1011" then
					DecodeOut <= "0100"; --4
				--R3
				elsif Row = "1101" then
					DecodeOut <= "0111"; --7
				--R4
				elsif Row = "1110" then
					DecodeOut <= "0000"; --0
				end if;
				sclk <= sclk+1;
			-- 2ms
			elsif sclk = "00110000110101000000" then	
				--C2
				Col<= "1011";
				sclk <= sclk+1;
			-- check row pins
			elsif sclk = "00110000110101001000" then	
				--R1
				if Row = "0111" then		
					DecodeOut <= "0010"; --2
				--R2
				elsif Row = "1011" then
					DecodeOut <= "0101"; --5
				--R3
				elsif Row = "1101" then
					DecodeOut <= "1000"; --8
				--R4
				elsif Row = "1110" then
					DecodeOut <= "1111"; --F
				end if;
				sclk <= sclk+1;	
			--3ms
			elsif sclk = "01001001001111100000" then 
				--C3
				Col<= "1101";
				sclk <= sclk+1;
			-- check row pins
			elsif sclk = "01001001001111101000" then 
				--R1
				if Row = "0111" then
					DecodeOut <= "0011"; --3	
				--R2
				elsif Row = "1011" then
					DecodeOut <= "0110"; --6
				--R3
				elsif Row = "1101" then
					DecodeOut <= "1001"; --9
				--R4
				elsif Row = "1110" then
					DecodeOut <= "1110"; --E
				end if;
				sclk <= sclk+1;
			--4ms
			elsif sclk = "01100001101010000000" then 			
				--C4
				Col<= "1110";
				sclk <= sclk+1;
			-- check row pins
			elsif sclk = "01100001101010001000" then 
				--R1
				if Row = "0111" then
					DecodeOut <= "1010"; --A
				--R2
				elsif Row = "1011" then
					DecodeOut <= "1011"; --B
				--R3
				elsif Row = "1101" then
					DecodeOut <= "1100"; --C
				--R4
				elsif Row = "1110" then
					DecodeOut <= "1101"; --D
				end if;
				sclk <= "00000000000000000000";	
			else
				sclk <= sclk+1;	
			end if;
		end if;
	end process;
		
		
						 
end Behavioral;

// VHDL entity F_DIV, as the project stores it:
LIBRARY ieee;
USE ieee.std_logic_1164.all;
USE ieee.std_logic_unsigned.all;

ENTITY F_DIV IS
	PORT(CLK_in,RESET: in std_logic;
		CLK_out: out std_logic);
END F_DIV;


ARCHITECTURE A OF F_DIV IS
BEGIN


PROCESS(CLK_in,RESET)
variable v: std_logic_vector(24 downto 0):=(others=>'0');
BEGIN

	if RESET='1' then
		v:=(others=>'0');
	else
		if CLK_in'EVENT and CLK_in='1' then
			v:=v+1;
		end if;
	end if;
	CLK_out<=v(24);

END PROCESS;
END A;

// VHDL entity DEBOUNCER, as the project stores it:
LIBRARY ieee;
USE ieee.std_logic_1164.all;

ENTITY DEBOUNCER IS
 	PORT (
BUTON,CLK: in std_logic;
 		Y: out std_logic);	
END DEBOUNCER;


ARCHITECTURE struct OF DEBOUNCER IS

COMPONENT DFF
	PORT (CLK,D,S,R: in std_logic;
  		Q: out std_logic);

END COMPONENT;

COMPONENT INP3_AND_GATE
	PORT(X1,X2,X3: in std_logic;
		Y: out std_logic);
END COMPONENT;

signal N1,N2,N3: std_logic;

BEGIN
C1: DFF port map (CLK,BUTON,'1','1',N1);
C2: DFF port map (CLK,N1,'1','1',N2);
C3: DFF port map (CLK,N2,'1','1',N3);
C4: INP3_AND_GATE port map (N1,N2,N3,Y);

END struct;

LIBRARY ieee;
USE ieee.std_logic_1164.all;
ENTITY DFF IS
	PORT (CLK,D,S,R: in std_logic;
  		Q: out std_logic);
END DFF;

ARCHITECTURE A OF DFF IS
BEGIN
D_Flip_Flop: process (CLK)
begin
	if CLK'EVENT and CLK='1' then
		if S='0'then
			Q<='1';
		else
			if R='0' then
				Q<='0';
			else
				Q<=D;
			end if;
		end if;
	end if;	
	
end process D_Flip_Flop;
END A;


LIBRARY ieee;
USE ieee.std_logic_1164.all;
ENTITY INP3_AND_GATE IS
	PORT(X1,X2,X3: in std_logic;
		Y: out std_logic);
END INP3_AND_GATE;

ARCHITECTURE behav OF INP3_AND_GATE IS
BEGIN
	Y<=X1 and X2 and X3;
END behav;

// VHDL entity display_unit, as the project stores it:
LIBRARY ieee;
USE ieee.std_logic_1164.all;
USE ieee.std_logic_unsigned.all; 
ENTITY display_unit IS
  PORT (
  data1, data2, data3,data4,data5,data6,data7,data8 : in std_logic_vector(6 downto 0);
  clk, reset: in std_logic;
  anodes: out std_logic_vector(7 downto 0);
  cathodes: out std_logic_vector(6 downto 0)
    );
END display_unit;

ARCHITECTURE TypeArchitecture OF DISPLAY_UNIT IS

signal new_clk: std_logic;
signal an: std_logic_vector(7 downto 0);

BEGIN

Frequency_divider: process(clk,reset)
	variable var: std_logic_vector(18 downto 0):=(others=>'0');
	begin
		if reset='1' then
			var:=(others=>'0');
		elsif clk'event and clk='1' then
			var:=var+1;
		end if;
	new_clk<=var(18);
	end process Frequency_divider;

Ring_Register_Anodes: process(new_clk)
	variable v: std_logic_vector(7 downto 0):="10000000";
	variable aux: std_logic;
	begin
	if new_clk'event and new_clk='1' then
		aux:=v(0);
		for i in 0 to 6 loop
			v(i):=v(i+1);
		end loop;
		v(7):=aux;
	end if;
	anodes<=v;
	an<=v;
	end process Ring_Register_Anodes;

Display: process(an,reset)
	variable x: std_logic_vector(6 downto 0);
	begin
	if reset='1' then
		case an is
			when "10000000" => x:="0000000";
			when "01000000" => x:="0000000";
			when "00100000" => x:="0000000";
			when others => x:="0000000";
		end case;
	else
		case an is
			when "10000000" => x:=data1;
			when "01000000" => x:=data2;
			when "00100000" => x:=data3;
			when "00010000" => x:=data4;
			when "00001000" => x:=data5;
			when "00000100" => x:=data6;
			when "00000010" => x:=data7;
			when "00000001" => x:=data8;
			when others => x:="0000000";
		end case;
	end if;
	cathodes<=x;

	end process Display;

END TypeArchitecture;

// VHDL entity BINARY_TO_7SEG, as the project stores it:
--------------------------------------------------------------------------------
-- Project :
-- File    :
-- Autor   :
-- Date    :
--
--------------------------------------------------------------------------------
-- Description :
--
--------------------------------------------------------------------------------

LIBRARY ieee;
USE ieee.std_logic_1164.all;

ENTITY BINARY_TO_7SEG IS
	PORT (binary_number: in std_logic_vector (3 downto 0);
		display_value: out std_logic_vector (6 downto 0));
END BINARY_TO_7SEG;

--------------------------------------------------------------------------------
--Complete your VHDL description below
--------------------------------------------------------------------------------

ARCHITECTURE A OF BINARY_TO_7SEG IS
BEGIN

	process(binary_number)
	variable v: std_logic_vector (6 downto 0);
	begin
		case binary_number is
			when "0000" => v:="1111110"; --abcdefg
			when "0001" => v:="0110000";
			when "0010" => v:="1101101";
			when "0011" => v:="1111001";
			when "0100" => v:="0110011";
			when "0101" => v:="1011011";
			when "0110" => v:="1011111";
			when "0111" => v:="1110000";
			when "1000" => v:="1111111";
			when "1001" => v:="1111011";
			when "1010" => v:="1110111";
			when "1011" => v:="0011111";
			when "1100" => v:="1001110";
			when "1101" => v:="0111101";
			when "1110" => v:="1001111";
			when others => v:="1000111";
		end case;
	display_value<=v;
	end process;
END A;

// VHDL entity store_data, as the project stores it:
LIBRARY ieee;
USE ieee.std_logic_1164.all;

ENTITY store_data IS
  PORT (
  reset: in std_logic;
  datain: in std_logic_vector(3 downto 0);
  addr: in std_logic_vector(3 downto 0);
  dataout: out std_logic_vector(31 downto 0)
  );
END store_data;


ARCHITECTURE TypeArchitecture OF store_data IS

BEGIN
process(datain, reset)
begin
if (reset = '1') then
dataout<= x"00000000";
else
if(addr = "0000") then
dataout(0)<= datain(0);
dataout(1)<= datain(1);
dataout(2)<= datain(2);
dataout(3)<= datain(3);
elsif(addr = "0001") then
dataout(4)<= datain(0);
dataout(5)<= datain(1);
dataout(6)<= datain(2);
dataout(7)<= datain(3);
elsif(addr = "0010") then
dataout(8)<= datain(0);
dataout(9)<= datain(1);
dataout(10)<= datain(2);
dataout(11)<= datain(3);
elsif(addr = "0011") then
dataout(12)<= datain(0);
dataout(13)<= datain(1);
dataout(14)<= datain(2);
dataout(15)<= datain(3);
elsif(addr = "0100") then
dataout(16)<= datain(0);
dataout(17)<= datain(1);
dataout(18)<= datain(2);
dataout(19)<= datain(3);
elsif(addr = "0101") then
dataout(20)<= datain(0);
dataout(21)<= datain(1);
dataout(22)<= datain(2);
dataout(23)<= datain(3);
elsif(addr = "0110") then
dataout(24)<= datain(0);
dataout(25)<= datain(1);
dataout(26)<= datain(2);
dataout(27)<= datain(3);
elsif(addr = "0111") then
dataout(28)<= datain(0);
dataout(29)<= datain(1);
dataout(30)<= datain(2);
dataout(31)<= datain(3);
end if;

end if;
end process;
END TypeArchitecture;

// VHDL entity decoder, as the project stores it:
LIBRARY ieee;
USE ieee.std_logic_1164.all;

ENTITY decoder IS
  PORT (
I0,I1,I2,I3,I4,I5,I6,I7,I8,I9,Ia,Ib, Ic, Id, Ie, Iff: in std_logic;
  		outp:out std_logic_vector(3 downto 0)
  
  );

END decoder;


ARCHITECTURE TypeArchitecture OF decoder IS

BEGIN

process(I0,I1,I2,I3,I4,I5,I6,I7,I8,I9,Ia,Ib, Ic, Id, Ie, Iff)
begin
if(I0 = '1') THEN
outp<= "0000";
elsif (I1 = '1') THEN
outp<= "0001";
elsif (I2 = '1') THEN
outp<= "0010";
elsif (I3 = '1') THEN
outp<= "0011";
elsif (I4 = '1') THEN
outp<= "0100";
elsif (I5 = '1') THEN
outp<= "0101";
elsif (I6 = '1') THEN
outp<= "0110";
elsif (I7 = '1') THEN
outp<= "0111";
elsif (I8 = '1') THEN
outp<= "1000";
elsif (I9 = '1') THEN
outp<= "1001";
elsif (Ia = '1') THEN
outp<= "1010";
elsif (Ib = '1') THEN
outp<= "1011";
elsif (Ic = '1') THEN
outp<= "1100";
elsif (Id = '1') THEN
outp<= "1101";
elsif (Ie = '1') THEN
outp<= "1110";
elsif (Iff = '1') THEN
outp<= "1111";
end if;
end process;

END TypeArchitecture;

// VHDL entity displayBASYS3, as the project stores it:
LIBRARY ieee;
USE ieee.std_logic_1164.all;

USE ieee.std_logic_unsigned.all; 
ENTITY displayBASYS3 IS
  PORT (
  data1, data2, data3,data4,data5,data6,data7,data8 : in std_logic_vector(6 downto 0);
  clk, reset: in std_logic;
  anodes: out std_logic_vector(3 downto 0);
  cathodes: out std_logic_vector(6 downto 0)
    );
END displayBASYS3;

ARCHITECTURE TypeArchitecture OF DISPLAYBASYS3 IS

signal new_clk: std_logic;
signal an: std_logic_vector(3 downto 0);

BEGIN

Frequency_divider: process(clk,reset)
	variable var: std_logic_vector(18 downto 0):=(others=>'0');
	begin
		if reset='1' then
			var:=(others=>'0');
		elsif clk'event and clk='1' then
			var:=var+1;
		end if;
	new_clk<=var(18);
	end process Frequency_divider;

Ring_Register_Anodes: process(new_clk)
	variable v: std_logic_vector(3 downto 0):="1000";
	variable aux: std_logic;
	begin
	if new_clk'event and new_clk='1' then
		aux:=v(0);
		for i in 0 to 2 loop
			v(i):=v(i+1);
		end loop;
		v(3):=aux;
	end if;
	anodes<=v;
	an<=v;
	end process Ring_Register_Anodes;

Display: process(an,reset)
	variable x: std_logic_vector(6 downto 0);
	begin
	if reset='1' then
		case an is
			when "1000" => x:="0000000";
			when "0100" => x:="0000000";
			when "0010" => x:="0000000";
			when others => x:="0000000";
		end case;
	else
		case an is
			when "1000" => x:=data1;
			when "0100" => x:=data2;
			when "0010" => x:=data3;
			when "0001" => x:=data4;
			when others => x:="0000000";
		end case;
	end if;
	cathodes<=x;

	end process Display;

END TypeArchitecture;

// VHDL entity F_DIV_new, as the project stores it:
LIBRARY ieee;
USE ieee.std_logic_1164.all;
USE ieee.std_logic_unsigned.all;

ENTITY F_DIV_new IS
	PORT(CLK_in,RESET: in std_logic;
		CLK_out: out std_logic);
END F_DIV_new;


ARCHITECTURE A OF F_DIV_new IS
BEGIN


PROCESS(CLK_in,RESET)
variable v: std_logic_vector(25 downto 0):=(others=>'0');
BEGIN

	if RESET='1' then
		v:=(others=>'0');
	else
		if CLK_in'EVENT and CLK_in='1' then
			v:=v+1;
		end if;
	end if;
	CLK_out<=v(25);

END PROCESS;
END A;
